// Logisim project alu.circ as structural Verilog: 1 circuit, main circuit main
module main (
  input  [7:0] A,
  input  [7:0] B,
  input  [2:0] S,
  output [7:0] Out,
  output ZF,
  output VF
);

  wire A_1_out, A_AND_B_out, A_B_out, A_OR_B_out, A_out, A_t, and_2_out, and_3_out, and_4_out, and_5_out,
       B_1_out, B_out, not_1_out, not_2_out, not_3_out, not_4_out, not_5_out, not_6_out, not_7_out,
       not_8_out, not_9_out, not_10_out, not_11_out, not_12_out, or_1_out, or_2_out, xor_1_out;
  wire [7:0] adder_1_out, and_1_out, not_13_out, or_3_out, transistor_1_out, transistor_3_out,
       transistor_4_out, transistor_5_out, transistor_8_out;

  not not_1 (not_1_out, S[2]);
  not not_2 (not_2_out, S[1]);
  not not_3 (not_3_out, S[0]);
  and u_A (A_out, not_1_out, not_2_out, not_3_out);
  not not_4 (not_4_out, S[2]);
  not not_5 (not_5_out, S[1]);
  and u_B (B_out, not_4_out, not_5_out, S[0]);
  not not_6 (not_6_out, S[2]);
  not not_7 (not_7_out, S[0]);
  and A_1 (A_1_out, not_6_out, S[1], not_7_out);
  not not_8 (not_8_out, S[2]);
  and B_1 (B_1_out, not_8_out, S[1], S[0]);
  not not_9 (not_9_out, S[1]);
  and A_B (A_B_out, S[2], not_9_out, not_10_out);
  not not_10 (not_10_out, S[0]);
  not not_11 (not_11_out, S[1]);
  and A_B_2 (A_t, S[2], not_11_out, S[0]);
  not not_12 (not_12_out, S[0]);
  and A_AND_B (A_AND_B_out, S[2], S[1], not_12_out);
  and A_OR_B (A_OR_B_out, S[2], S[1], S[0]);
  or or_1 (or_1_out, A_out, A_1_out, A_B_out, A_t);
  or or_2 (or_2_out, B_out, B_1_out, A_B_out, A_t);
  Transistor #(.\type ("n"), .gate("br"), .width(8)) transistor_1 (.in(B), .out(transistor_1_out), .gate(or_2_out));
  Transistor #(.width(8)) transistor_2 (.in({8{1'b0}}), .out(transistor_1_out), .gate(or_2_out));
  assign and_1_out = B & A;  // AND_Gate and_1, 8 bits wide
  assign or_3_out = B | A;  // OR_Gate or_3, 8 bits wide
  Transistor #(.\type ("n"), .width(8)) transistor_3 (.in(and_1_out), .out(transistor_3_out), .gate(A_AND_B_out));
  Transistor #(.\type ("n"), .width(8)) transistor_4 (.in(or_3_out), .out(transistor_4_out), .gate(A_OR_B_out));
  Transistor #(.width(8)) transistor_5 (.in({8{1'b0}}), .out(transistor_5_out), .gate(or_1_out));
  Transistor #(.\type ("n"), .gate("br"), .width(8)) transistor_6 (.in(A), .out(transistor_5_out), .gate(or_1_out));
  Transistor #(.width(8)) transistor_7 (.in({8{1'b0}}), .out(transistor_4_out), .gate(A_OR_B_out));
  Transistor #(.gate("br"), .width(8)) transistor_8 (.in(transistor_1_out), .out(transistor_8_out), .gate(A_t));
  Transistor #(.\type ("n"), .width(8)) transistor_9 (.in(not_13_out), .out(transistor_8_out), .gate(A_t));
  assign not_13_out = ~transistor_1_out;  // NOT_Gate not_13, 8 bits wide
  Transistor #(.width(8)) transistor_10 (.in({8{1'b0}}), .out(transistor_3_out), .gate(A_AND_B_out));
  and and_2 (and_2_out, ~transistor_5_out[7], ~transistor_8_out[7]);  // AND_Gate
  and and_3 (and_3_out, transistor_5_out[7], transistor_8_out[7]);
  and and_4 (and_4_out, and_3_out, ~Out[7]);  // AND_Gate
  or or_4 (VF, and_4_out, and_5_out);
  ExactlyOne xor_1 (.out(xor_1_out), .in1(A_1_out), .in2(B_1_out), .in3(A_t));
  Adder adder_1 (.a(transistor_5_out), .b(transistor_8_out), .out(adder_1_out), .cin(xor_1_out));  // open: cout
  and and_5 (and_5_out, and_2_out, Out[7]);
  assign Out = adder_1_out | transistor_3_out | transistor_4_out;  // OR_Gate or_5, 8 bits wide
  nor nor_1 (ZF, Out[7], Out[6], Out[5], Out[4], Out[3], Out[2], Out[1], Out[0]);
endmodule
